# Fritzing sketch PCLapCounterHW (saved by Fritzing 0.9.3b)
breadboards: 1

parts:
  Part1 = Arduino Mega 2560 (Rev3)
  FS_0_3 = Hexadecimal Rotary Encoder [part_number=APEM-PT65-303 package=THT]
  LED_FS_3 = LED - 5mm [color="Red (633nm)" package="5 mm [THT]"]
  LED_FS_2 = LED - 5mm [color="Red (633nm)" package="5 mm [THT]"]
  LED_FS_1 = LED - 5mm [color="Red (633nm)" package="5 mm [THT]"]
  LED_FS_0 = LED - 5mm [color="Red (633nm)" package="5 mm [THT]"]
  R_FS_0_3 = Resistor [tolerance=±5% resistance=10k package="0402 [SMD]"]
  pauseRace = Pushbutton [package=THT]
  togglePower = Pushbutton [package=THT]
  startPauseRestartRace = Pushbutton [package=THT]
  LED_IR_1 = LED - 5mm [color="Infrared (940nm)" package="5 mm [THT]"]
  LED_IR_2 = LED - 5mm [color="Infrared (940nm)" package="5 mm [THT]"]
  LED_IR_3 = LED - 5mm [color="Infrared (940nm)" package="5 mm [THT]"]
  LED_IR_4 = LED - 5mm [color="Infrared (940nm)" package="5 mm [THT]"]
  LED_IR_5 = LED - 5mm [color="Infrared (940nm)" package="5 mm [THT]"]
  LED_IR_6 = LED - 5mm [color="Infrared (940nm)" package="5 mm [THT]"]
  LED_IR_VISIBLE = LED - 5mm [color="Red (633nm)" package="5 mm [THT]"]
  START_1 = LED - 5mm [color="Red (633nm)" package="5 mm [THT]"]
  START_2 = LED - 5mm [color="Red (633nm)" package="5 mm [THT]"]
  START_3 = LED - 5mm [color="Red (633nm)" package="5 mm [THT]"]
  START_4 = LED - 5mm [color="Red (633nm)" package="5 mm [THT]"]
  START_5 = LED - 5mm [color="Red (633nm)" package="5 mm [THT]"]
  R_START_1 = Resistor [tolerance=±5% resistance=1k package="0402 [SMD]"]
  R_START_2 = Resistor [tolerance=±5% resistance=1k package="0402 [SMD]"]
  R_START_3 = Resistor [tolerance=±5% resistance=1k package="0402 [SMD]"]
  R_START_4 = Resistor [tolerance=±5% resistance=1k package="0402 [SMD]"]
  R_START_5 = Resistor [tolerance=±5% resistance=1k package="0402 [SMD]"]
  LED_GO = LED - 5mm [color="Green (560nm)" package="5 mm [THT]"]
  LED_STOP = LED - 5mm [color="Red (633nm)" package="5 mm [THT]"]
  R_GO = Resistor [tolerance=±5% resistance=1k package="0402 [SMD]"]
  R_STOP = Resistor [tolerance=±5% resistance=1k package="0402 [SMD]"]
  LED_PWR_ALL = LED - 5mm [color="Orange (620nm)" package="5 mm [THT]"]
  R_PWR_ALL = Resistor [tolerance=±5% resistance=1k package="0402 [SMD]"]
  Q8 = PNP-Transistor [package="TO92 [THT]"]
  R_PWR_9 = Resistor [tolerance=±5% resistance=1k package="0402 [SMD]"]
  Q9 = LTR-301 [package=ltr-301]
  WeMos_D1_Mini_Relay_Shield_V3 = WeMos D1 Mini Relay Shield V2  # not connected

nets:
  N1: Part1.D11_PWM, LED_STOP.cathode
  N2: Part1.D10_PWM, LED_GO.cathode
  N3: Part1.D9_PWM, START_1.cathode
  N4: Part1.D8_PWM, START_2.cathode
  N5: Part1.5V, R_FS_0_3.Pin_0, R_START_1.Pin_1, R_START_2.Pin_1, R_START_3.Pin_1, R_START_4.Pin_1, R_START_5.Pin_1, R_GO.Pin_1, R_STOP.Pin_1, R_PWR_ALL.Pin_1
  N6: Part1.GND, FS_0_3.InputCommon, pauseRace.leg1, togglePower.leg1, startPauseRestartRace.leg1
  N7: Part1.D5_PWM, START_5.cathode
  N8: Part1.D6_PWM, START_4.cathode
  N9: Part1.D7_PWM, START_3.cathode
  N10: Part1.D22, FS_0_3.Output1Pin, LED_FS_0.cathode
  N11: Part1.D23, FS_0_3.Output2Pin, LED_FS_1.cathode
  N12: Part1.D24, FS_0_3.Output4Pin, LED_FS_2.cathode
  N13: Part1.D25, FS_0_3.Output8pin, LED_FS_3.cathode
  N14: Part1.D30, LED_PWR_ALL.cathode
  N15: Part1.D43, pauseRace.leg0
  N16: Part1.D44, startPauseRestartRace.leg0
  N17: Part1.D48, togglePower.leg0
  N18: LED_FS_3.anode, LED_FS_2.anode, LED_FS_1.anode, LED_FS_0.anode, R_FS_0_3.Pin_1
  N19: LED_IR_1.cathode, LED_IR_2.anode
  N20: LED_IR_1.anode, LED_IR_VISIBLE.cathode
  N21: LED_IR_2.cathode, LED_IR_3.anode
  N22: LED_IR_3.cathode, LED_IR_4.anode
  N23: LED_IR_4.cathode, LED_IR_5.anode
  N24: LED_IR_5.cathode, LED_IR_6.anode
  N25: START_1.anode, R_START_1.Pin_0
  N26: START_2.anode, R_START_2.Pin_0
  N27: START_3.anode, R_START_3.Pin_0
  N28: START_4.anode, R_START_4.Pin_0
  N29: START_5.anode, R_START_5.Pin_0
  N30: LED_GO.anode, R_GO.Pin_0
  N31: LED_STOP.anode, R_STOP.Pin_0
  N32: LED_PWR_ALL.anode, R_PWR_ALL.Pin_0
  N33: Q8.B, R_PWR_9.Pin_0
  N34: Q8.C, Q9.C
  N35: R_PWR_9.Pin_1, Q9.E

notes:
  30mA constant current source
  photo diodes wired to 6 interrupt pins
  trigger: RISING
  False Start Init
  Starting Lights
  Stop / Go Lights
  PWR ALL
  PWR LANE #
  USB to PC with PC Lap Counter
  to pin
  IR sensor wiring
  to GND
  See IR sensor wiring
  to relays pin
  5V power supply
  driving the 6 relays
  Race power supply
  Track
  Controller
  Connect the track wire between controller and track to the "normally connected" (NC) terminal.
  Connect the track plus to the middle terminal.
  This allows for driving cars without the need of any other HW and SW to be active.
  When the power to the track is off, the lane will be forced to break. The plus and minus leads of the track are connected which shorts the motor and breaking is automatic. Your cars no longer will fly off the track when the power goes off.
  Additionally, your controller will always be powered which can be an advantage, certainly for some electronic ones.
